# Fritzing sketch IrrigationCircuit (saved by Fritzing 1.0.4)

parts:
  esp1 = ESP32 DevKitc V4
  S2 = Pushbutton [package=THT]
  RL6 = Solid State High Level Relay Module [package=relay]
  S1 = Pushbutton [package=THT]
  S3 = Pushbutton [package=THT]
  S6 = Pushbutton [package=THT]
  S7 = Pushbutton [package=THT]
  S9 = Pushbutton [package=THT]
  S5 = Pushbutton [package=THT]
  S4 = Pushbutton [package=THT]
  S8 = Pushbutton [package=THT]
  RL3 = Solid State High Level Relay Module [package=relay]
  RL2 = Solid State High Level Relay Module [package=relay]
  RL1 = Solid State High Level Relay Module [package=relay]
  RL5 = Solid State High Level Relay Module [package=relay]
  RL4 = Solid State High Level Relay Module [package=relay]
  RL8 = Solid State High Level Relay Module [package=relay]
  RL7 = Solid State High Level Relay Module [package=relay]
  RL9 = Solid State High Level Relay Module [package=relay]
  VALVE1 = Plastic Solenoid Valve
  R3 = Resistor [tolerance=±5% power=0.25W resistance=220 package=THT]
  R4 = Resistor [tolerance=±5% power=0.25W resistance=220 package=THT]

nets:
  N1: esp1.IO15, S3.leg0
  N2: esp1.IO2, S4.leg0
  N3: esp1.IO4, S5.leg0
  N4: esp1.IO16, S6.leg0
  N5: esp1.IO17, S7.leg0
  N6: esp1.IO5, S8.leg0
  N7: esp1.IO18, S9.leg0
  N8: esp1.IO19, RL9.CH1
  N9: esp1.IO21, RL8.CH1
  N10: esp1.IO22, RL7.CH1
  N11: esp1.IO23, RL6.CH1
  N12: esp1.3V3, S2.leg1, S1.leg1, S3.leg1, S6.leg1, S7.leg1, S9.leg1, S5.leg1, S4.leg1, S8.leg1
  N13: esp1.IO35, R3.Pin_0
  N14: esp1.IO32, RL5.CH1
  N15: esp1.IO33, RL4.CH1
  N16: esp1.IO25, RL3.CH1
  N17: esp1.IO26, RL2.CH1
  N18: esp1.IO27, RL1.CH1
  N19: esp1.IO14, S1.leg0
  N20: esp1.IO13, S2.leg0
  N21: RL1.B1, VALVE1.no_name_yet
  N22: R3.Pin_1, R4.Pin_0

custom parts:
  ESP32 DevKitc V4: ESP32-DevKitC board with ESP32-WROOM-32 module. ESP32-DevKitC V4 is a small-sized ESP32-based development board produced by Espressif. Most of the pins on the ESP module are broken out to the pin headers on the board. The pins D0, D1, D2, D3, CMD and CLK are used internally for communication between ESP32 and SPI flash memory. They are grouped on both sides near the USB connector. Avoid using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
  Solid State High Level Relay Module: 5V Omron solid state relay 240V 2A output with resistance fuse.
